// Logisim project alu.circ as structural Verilog: 1 circuit, main circuit alu
module alu (
  input  [31:0] A,
  input  [31:0] B,
  input  [3:0] ALUSel,
  output [31:0] ALUResult
);

  wire comparator_1_lt;
  wire [4:0] bit_extender_1_out, bit_extender_2_out, bit_extender_3_out;
  wire [31:0] add, ant, exclusiveOr, mul, mulh, mulhu, oar, setLessThan, shiftLeftLogical,
       shiftRightArithmetic, shiftRightLogical, sub;

  Bit_Extender #(.in_width(32), .out_width(5)) bit_extender_1 (.in(B), .out(bit_extender_1_out));
  Bit_Extender #(.in_width(32), .out_width(5)) bit_extender_2 (.in(B), .out(bit_extender_2_out));
  Bit_Extender #(.in_width(32), .out_width(5)) bit_extender_3 (.in(B), .out(bit_extender_3_out));
  Adder #(.width(32)) adder_1 (.a(A), .b(B), .out(add));  // open: cin, cout
  Shifter #(.width(32)) shifter_1 (.in(A), .\dist (bit_extender_1_out), .out(shiftLeftLogical));
  Comparator #(.width(32)) comparator_1 (.a(A), .b(B), .lt(comparator_1_lt));  // open: gt, eq
  assign exclusiveOr = A ^ B;  // XOR_Gate xor_1, 32 bits wide
  Shifter #(.shift("lr"), .width(32)) shifter_2 (.in(A), .\dist (bit_extender_2_out), .out(shiftRightLogical));
  assign oar = A | B;  // OR_Gate or_1, 32 bits wide
  assign ant = A & B;  // AND_Gate and_1, 32 bits wide
  Multiplier #(.mode("twosComplement"), .width(32)) multiplier_1 (.a(A), .b(B), .out(mul), .cout(mulh));  // open: cin
  Multiplier #(.width(32)) multiplier_2 (.a(A), .b(B), .cout(mulhu));  // open: out, cin
  Subtractor #(.width(32)) subtractor_1 (.a(A), .b(B), .out(sub));  // open: bin, bout
  Shifter #(.shift("ar"), .width(32)) shifter_3 (.in(A), .\dist (bit_extender_3_out), .out(shiftRightArithmetic));
  assign setLessThan = {{31{1'b0}}, comparator_1_lt};  // Bit_Extender bit_extender_4
  Multiplexer #(.select(4), .width(32)) multiplexer_1 (
    .in0(add), .in1(shiftLeftLogical), .in2(setLessThan), .in4(exclusiveOr), .in5(shiftRightLogical),
    .in6(oar), .in7(ant), .in8(mul), .in9(mulh), .in11(mulhu), .in12(sub), .in13(shiftRightArithmetic),
    .in15(B), .out(ALUResult), .sel(ALUSel));  // open: in3, in10, in14

  // Notes on the sheet:
  //   INPUTS to your circuit
  //   DON'T CHANGE THE LOCATIONS OF THE INPUTS AND OUTPUTS!
  //   OUTPUT from your circuit
endmodule
