// Logisim project partial-store.circ as structural Verilog: 1 circuit, main circuit partial_store
module partial_store (
  input  [31:0] Instruction,
  input  [31:0] MemAddress,
  input  [31:0] DataFromReg,
  input  MemWEn,
  output [3:0] MemWriteMask,
  output [31:0] DataToMem
);

  wire comparator_1_eq, comparator_1_gt, comparator_1_lt, comparator_2_eq;
  wire [1:0] priority_encoder_1_out, sh_offset;
  wire [3:0] shifter_1_out, shifter_2_out;
  wire [31:0] multiplexer_2_out, multiplexer_3_out;

  assign sh_offset = 2'b10 & MemAddress[1:0];  // AND_Gate and_1, 2 bits wide
  Comparator #(.mode("unsigned"), .width(3)) comparator_1 (
    .a(Instruction[14:12]), .b(3'b001), .gt(comparator_1_gt), .eq(comparator_1_eq), .lt(comparator_1_lt));
  Priority_Encoder #(.select_enc(2)) priority_encoder_1 (
    .in0(comparator_1_gt), .in1(comparator_1_eq), .in2(comparator_1_lt), .out(priority_encoder_1_out),
    .en_in(MemWEn));  // open: in3, gs, en_out
  Shifter #(.width(4)) shifter_1 (.in(4'b0011), .\dist (sh_offset), .out(shifter_1_out));
  Shifter #(.width(4)) shifter_2 (.in(4'b0001), .\dist (MemAddress[1:0]), .out(shifter_2_out));
  Multiplexer #(.enable("true"), .select(2), .width(4)) multiplexer_1 (
    .in0(4'b1111), .in1(shifter_1_out), .in2(shifter_2_out), .out(MemWriteMask),
    .sel(priority_encoder_1_out), .en(MemWEn));  // open: in3
  Comparator #(.width(2)) comparator_2 (.a(sh_offset), .b(2'b10), .eq(comparator_2_eq));  // open: gt, lt
  Multiplexer #(.width(32)) multiplexer_2 (
    .in0({{16{1'b0}}, DataFromReg[15:0]}), .in1({DataFromReg[15:0], {16{1'b0}}}), .out(multiplexer_2_out),
    .sel(comparator_2_eq));
  Multiplexer #(.select(2), .width(32)) multiplexer_3 (
    .in0({{24{1'b0}}, DataFromReg[7:0]}), .in1({{16{1'b0}}, DataFromReg[7:0], {8{1'b0}}}),
    .in2({{8{1'b0}}, DataFromReg[7:0], {16{1'b0}}}), .in3({DataFromReg[7:0], {24{1'b0}}}),
    .out(multiplexer_3_out), .sel(MemAddress[1:0]));
  Multiplexer #(.select(2), .width(32)) multiplexer_4 (
    .in0(DataFromReg), .in1(multiplexer_2_out), .in2(multiplexer_3_out), .out(DataToMem),
    .sel(priority_encoder_1_out));  // open: in3

  // Other names for the same wires on the sheet: funct3[2:0] = Instruction[14:12]; bottom[1:0] = MemAddress[1:0]

  // Notes on the sheet:
  //   INPUTS to your circuit
  //   DON'T CHANGE THE LOCATIONS OF THE INPUTS AND OUTPUTS!
  //   OUTPUT from your circuit
endmodule
