// Logisim project regfile.circ as structural Verilog: 1 circuit, main circuit regfile
// ex0
module regfile (
  input  [4:0] ReadIndex1,
  input  [4:0] ReadIndex2,
  input  [4:0] WriteIndex,
  input  [31:0] WriteData,
  input  RegWEn,
  input  clk,
  output [31:0] ra,
  output [31:0] sp,
  output [31:0] t0,
  output [31:0] t1,
  output [31:0] t2,
  output [31:0] s0,
  output [31:0] s1,
  output [31:0] a0,
  output [31:0] ReadData1,
  output [31:0] ReadData2
);

  wire a0_write, a1_write, a2_write, a3_write, a4_write, a5_write, a6_write, a7_write, gp_write, ra_write,
       s0_write, s1_write, s2_write, s3_write, s4_write, s5_write, s6_write, s7_write, s8_write, s9_write,
       s10_write, s11_write, sp_write, t0_write, t1_write, t2_write, t3_write, t4_write, t5_write, t6_write,
       tp_write;
  wire [31:0] a1, a2, a3, a4, a5, a6, a7, gp, s2, s3, s4, s5, s6, s7, s8, s9, s10, s11, t3, t4, t5, t6, tp;

  Register #(.width(32)) register_1 (.D(WriteData), .en(ra_write), .clk(clk), .Q(ra));  // open: clr
  Register #(.width(32)) register_2 (.D(WriteData), .en(sp_write), .clk(clk), .Q(sp));  // open: clr
  Register #(.width(32)) register_3 (.D(WriteData), .en(gp_write), .clk(clk), .Q(gp));  // open: clr
  Register #(.width(32)) register_4 (.D(WriteData), .en(tp_write), .clk(clk), .Q(tp));  // open: clr
  Register #(.width(32)) register_5 (.D(WriteData), .en(t0_write), .clk(clk), .Q(t0));  // open: clr
  Register #(.width(32)) register_6 (.D(WriteData), .en(t1_write), .clk(clk), .Q(t1));  // open: clr
  Register #(.width(32)) register_7 (.D(WriteData), .en(t2_write), .clk(clk), .Q(t2));  // open: clr
  Register #(.width(32)) register_8 (.D(WriteData), .en(s0_write), .clk(clk), .Q(s0));  // open: clr
  Register #(.width(32)) register_9 (.D(WriteData), .en(s1_write), .clk(clk), .Q(s1));  // open: clr
  Register #(.width(32)) register_10 (.D(WriteData), .en(a0_write), .clk(clk), .Q(a0));  // open: clr
  Register #(.width(32)) register_11 (.D(WriteData), .en(a6_write), .clk(clk), .Q(a6));  // open: clr
  Register #(.width(32)) register_12 (.D(WriteData), .en(a5_write), .clk(clk), .Q(a5));  // open: clr
  Register #(.width(32)) register_13 (.D(WriteData), .en(a3_write), .clk(clk), .Q(a3));  // open: clr
  Register #(.width(32)) register_14 (.D(WriteData), .en(a2_write), .clk(clk), .Q(a2));  // open: clr
  Register #(.width(32)) register_15 (.D(WriteData), .en(a1_write), .clk(clk), .Q(a1));  // open: clr
  Demultiplexer #(.select(5)) demultiplexer_1 (
    .out1(ra_write), .out2(sp_write), .out3(gp_write), .out4(tp_write), .out5(t0_write), .out6(t1_write),
    .out7(t2_write), .out8(s0_write), .out9(s1_write), .out10(a0_write), .out11(a1_write), .out12(a2_write),
    .out13(a3_write), .out14(a4_write), .out15(a5_write), .out16(a6_write), .out17(a7_write),
    .out18(s2_write), .out19(s3_write), .out20(s4_write), .out21(s5_write), .out22(s6_write),
    .out23(s7_write), .out24(s8_write), .out25(s9_write), .out26(s10_write), .out27(s11_write),
    .out28(t3_write), .out29(t4_write), .out30(t5_write), .out31(t6_write), .in(RegWEn), .sel(WriteIndex));  // open: out0
  Register #(.width(32)) register_16 (.D(WriteData), .en(a4_write), .clk(clk), .Q(a4));  // open: clr
  Register #(.width(32)) register_17 (.D(WriteData), .en(a7_write), .clk(clk), .Q(a7));  // open: clr
  Register #(.width(32)) register_18 (.D(WriteData), .en(s2_write), .clk(clk), .Q(s2));  // open: clr
  Register #(.width(32)) register_19 (.D(WriteData), .en(s3_write), .clk(clk), .Q(s3));  // open: clr
  Register #(.width(32)) register_20 (.D(WriteData), .en(s4_write), .clk(clk), .Q(s4));  // open: clr
  Register #(.width(32)) register_21 (.D(WriteData), .en(s5_write), .clk(clk), .Q(s5));  // open: clr
  Register #(.width(32)) register_22 (.D(WriteData), .en(s6_write), .clk(clk), .Q(s6));  // open: clr
  Register #(.width(32)) register_23 (.D(WriteData), .en(s7_write), .clk(clk), .Q(s7));  // open: clr
  Register #(.width(32)) register_24 (.D(WriteData), .en(s8_write), .clk(clk), .Q(s8));  // open: clr
  Register #(.width(32)) register_25 (.D(WriteData), .en(s9_write), .clk(clk), .Q(s9));  // open: clr
  Register #(.width(32)) register_26 (.D(WriteData), .en(s10_write), .clk(clk), .Q(s10));  // open: clr
  Register #(.width(32)) register_27 (.D(WriteData), .en(s11_write), .clk(clk), .Q(s11));  // open: clr
  Register #(.width(32)) register_28 (.D(WriteData), .en(t3_write), .clk(clk), .Q(t3));  // open: clr
  Register #(.width(32)) register_29 (.D(WriteData), .en(t4_write), .clk(clk), .Q(t4));  // open: clr
  Register #(.width(32)) register_30 (.D(WriteData), .en(t5_write), .clk(clk), .Q(t5));  // open: clr
  Register #(.width(32)) register_31 (.D(WriteData), .en(t6_write), .clk(clk), .Q(t6));  // open: clr
  Multiplexer #(.select(5), .width(32)) multiplexer_1 (
    .in0({32{1'b0}}), .in1(ra), .in2(sp), .in3(gp), .in4(tp), .in5(t0), .in6(t1), .in7(t2), .in8(s0),
    .in9(s1), .in10(a0), .in11(a1), .in12(a2), .in13(a3), .in14(a4), .in15(a5), .in16(a6), .in17(a7),
    .in18(s2), .in19(s3), .in20(s4), .in21(s5), .in22(s6), .in23(s7), .in24(s8), .in25(s9), .in26(s10),
    .in27(s11), .in28(t3), .in29(t4), .in30(t5), .in31(t6), .out(ReadData1), .sel(ReadIndex1));
  Multiplexer #(.select(5), .width(32)) multiplexer_2 (
    .in0({32{1'b0}}), .in1(ra), .in2(sp), .in3(gp), .in4(tp), .in5(t0), .in6(t1), .in7(t2), .in8(s0),
    .in9(s1), .in10(a0), .in11(a1), .in12(a2), .in13(a3), .in14(a4), .in15(a5), .in16(a6), .in17(a7),
    .in18(s2), .in19(s3), .in20(s4), .in21(s5), .in22(s6), .in23(s7), .in24(s8), .in25(s9), .in26(s10),
    .in27(s11), .in28(t3), .in29(t4), .in30(t5), .in31(t6), .out(ReadData2), .sel(ReadIndex2));

  // Notes on the sheet:
  //   INPUTS to your circuit
  //   DON'T CHANGE THE LOCATIONS OF THE INPUTS AND OUTPUTS!
  //   These are DEBUG/TEST outputs from your circuit.
  //   OUTPUTS from your circuit
endmodule
